# Fritzing sketch lightcontroller (saved by Fritzing 0.9.2b)
breadboards: 1

parts:
  J1 = female pin header, 14 pins [form="♀ (female)"]
  J2 = female pin header, 14 pins [form="♀ (female)"]
  Q1 = MOSFET-NCHANNEL [package=to220v]
  Q2 = MOSFET-NCHANNEL [package=to220v]
  Q3 = MOSFET-NCHANNEL [package=to220v]
  Q4 = MOSFET-NCHANNEL [package=to220v]
  J3 = female pin header, 5 pins [form="♀ (female)"]
  R1 = Rotary Potentiometer (Small) [maximum_resistance=100kΩ package=THT]
  JACK1 = 2.1mm Barrel Jack with Terminal Block
  R2 = Rotary Potentiometer (Small) [maximum_resistance=100kΩ package=THT]
  R3 = Rotary Potentiometer (Small) [maximum_resistance=100kΩ package=THT]
  R4 = Rotary Potentiometer (Small) [maximum_resistance=100kΩ package=THT]

nets:
  N1: J1.pin5, Q3.G
  N2: J1.pin8, Q2.G
  N3: J1.pin9, Q1.G
  N4: J1.pin11, Q4.G
  N5: J2.pin4, J3.pin5, R1.leg1
  N6: J2.pin10, R4.wiper
  N7: J2.pin11, R3.wiper
  N8: J2.pin12, R2.wiper
  N9: J2.pin13, R1.wiper
  N10: Q1.D, J3.pin2
  N11: Q1.S, Q2.S, Q3.S, Q4.S, J3.pin4, R1.leg2, JACK1.NEG
  N12: Q2.D, J3.pin1
  N13: Q4.D, J3.pin3
